// Logisim project Digital clock.circ as structural Verilog: 2 circuits, main circuit b2d
module main (
  output out_1,
  output out_2,
  output out_3,
  output out_4,
  output out_5,
  output out_6,
  output out_7,
  output out_8,
  output out_9,
  output out_10,
  output out_11,
  output out_12,
  output out_13,
  output out_14,
  output out_15,
  output out_16,
  output out_17,
  output out_18,
  output out_19,
  output out_20,
  output out_21,
  output out_22,
  output out_23,
  output out_24
);

  wire and_1_out, and_2_out, and_3_out, and_4_out, and_5_out, and_6_out, and_7_out, and_8_out, and_9_out,
       and_10_out, and_11_out, b2d_1_a_2, b2d_1_b_2, b2d_1_c_2, b2d_1_d_2, b2d_1_e, b2d_1_f, b2d_1_g,
       b2d_2_a_2, b2d_2_b_2, b2d_2_c_2, b2d_2_d_2, b2d_2_e, b2d_2_f, b2d_2_g, b2d_3_a_2, b2d_3_b_2,
       b2d_3_c_2, b2d_3_d_2, b2d_3_e, b2d_3_f, b2d_3_g, b2d_4_a_2, b2d_4_b_2, b2d_4_c_2, b2d_4_d_2, b2d_4_e,
       b2d_4_f, b2d_4_g, b2d_5_a_2, b2d_5_b_2, b2d_5_c_2, b2d_5_d_2, b2d_5_e, b2d_5_f, b2d_5_g, b2d_6_a_2,
       b2d_6_b_2, b2d_6_c_2, b2d_6_d_2, b2d_6_e, b2d_6_f, b2d_6_g, clock_1_out, not_1_out, not_2_out,
       not_3_out, not_4_out, not_5_out, not_6_out, not_7_out, not_8_out, not_9_out, not_10_out, not_11_out,
       not_12_out, not_13_out, not_14_out, not_15_out, or_1_out;

  Clock clock_1 (.out(clock_1_out));
  Counter #(.width(4), .max('ha)) counter_1 (
    .Q({out_1, out_2, out_3, out_4}), .clk(clock_1_out), .clr(and_6_out));  // open: load, D, count, carry
  Counter #(.width(4), .max('ha)) counter_2 (
    .Q({out_5, out_6, out_7, out_8}), .clk(and_1_out), .clr(and_7_out));  // open: load, D, count, carry
  Counter #(.width(4), .max('ha)) counter_3 (
    .Q({out_9, out_10, out_11, out_12}), .clk(and_2_out), .clr(and_8_out));  // open: load, D, count, carry
  Counter #(.width(4), .max('ha)) counter_4 (
    .Q({out_13, out_14, out_15, out_16}), .clk(and_3_out), .clr(and_9_out));  // open: load, D, count, carry
  Counter #(.width(4), .max('ha)) counter_5 (
    .Q({out_17, out_18, out_19, out_20}), .clk(and_4_out), .clr(or_1_out));  // open: load, D, count, carry
  Counter #(.width(4), .max('ha)) counter_6 (
    .Q({out_21, out_22, out_23, out_24}), .clk(and_5_out), .clr(and_11_out));  // open: load, D, count, carry
  and and_1 (and_1_out, out_1, out_3);
  and and_2 (and_2_out, out_6, out_7);
  and and_3 (and_3_out, out_9, out_11);
  and and_4 (and_4_out, out_14, out_15);
  and and_5 (and_5_out, out_17, out_19);
  or or_1 (or_1_out, and_10_out, and_11_out);
  and and_6 (and_6_out, not_10_out, out_3, not_4_out, out_1);
  and and_7 (and_7_out, not_5_out, out_7, out_6, not_1_out);
  and and_8 (and_8_out, not_11_out, out_11, not_6_out, out_9);
  and and_9 (and_9_out, not_12_out, out_15, out_14, not_2_out);
  and and_10 (and_10_out, not_13_out, out_19, not_7_out, out_17);
  and and_11 (and_11_out, not_3_out, not_13_out, out_18, not_14_out, not_15_out, out_23, not_8_out, not_9_out);
  not not_1 (not_1_out, out_5);
  not not_2 (not_2_out, out_13);
  not not_3 (not_3_out, out_17);
  not not_4 (not_4_out, out_2);
  not not_5 (not_5_out, out_8);
  not not_6 (not_6_out, out_10);
  not not_7 (not_7_out, out_18);
  not not_8 (not_8_out, out_22);
  not not_9 (not_9_out, out_21);
  not not_10 (not_10_out, out_4);
  not not_11 (not_11_out, out_12);
  not not_12 (not_12_out, out_16);
  not not_13 (not_13_out, out_20);
  not not_14 (not_14_out, out_19);
  not not_15 (not_15_out, out_24);
  b2d b2d_1 (
    .D(out_1), .C(out_2), .B(out_3), .A(out_4), .a_2(b2d_1_a_2), .b_2(b2d_1_b_2), .c_2(b2d_1_c_2),
    .d_2(b2d_1_d_2), .e(b2d_1_e), .f(b2d_1_f), .g(b2d_1_g));
  b2d b2d_2 (
    .D(out_5), .C(out_6), .B(out_7), .A(out_8), .a_2(b2d_2_a_2), .b_2(b2d_2_b_2), .c_2(b2d_2_c_2),
    .d_2(b2d_2_d_2), .e(b2d_2_e), .f(b2d_2_f), .g(b2d_2_g));
  b2d b2d_3 (
    .D(out_9), .C(out_10), .B(out_11), .A(out_12), .a_2(b2d_3_a_2), .b_2(b2d_3_b_2), .c_2(b2d_3_c_2),
    .d_2(b2d_3_d_2), .e(b2d_3_e), .f(b2d_3_f), .g(b2d_3_g));
  b2d b2d_4 (
    .D(out_13), .C(out_14), .B(out_15), .A(out_16), .a_2(b2d_4_a_2), .b_2(b2d_4_b_2), .c_2(b2d_4_c_2),
    .d_2(b2d_4_d_2), .e(b2d_4_e), .f(b2d_4_f), .g(b2d_4_g));
  b2d b2d_5 (
    .D(out_17), .C(out_18), .B(out_19), .A(out_20), .a_2(b2d_5_a_2), .b_2(b2d_5_b_2), .c_2(b2d_5_c_2),
    .d_2(b2d_5_d_2), .e(b2d_5_e), .f(b2d_5_f), .g(b2d_5_g));
  b2d b2d_6 (
    .D(out_21), .C(out_22), .B(out_23), .A(out_24), .a_2(b2d_6_a_2), .b_2(b2d_6_b_2), .c_2(b2d_6_c_2),
    .d_2(b2d_6_d_2), .e(b2d_6_e), .f(b2d_6_f), .g(b2d_6_g));
  _7_Segment_Display u_7_segment_display_1 (
    .g(b2d_2_g), .f(b2d_2_f), .a(b2d_2_a_2), .b(b2d_2_b_2), .e(b2d_2_e), .d(b2d_2_d_2), .c(b2d_2_c_2));  // open: dp
  _7_Segment_Display u_7_segment_display_2 (
    .g(b2d_1_g), .f(b2d_1_f), .a(b2d_1_a_2), .b(b2d_1_b_2), .e(b2d_1_e), .d(b2d_1_d_2), .c(b2d_1_c_2));  // open: dp
  _7_Segment_Display u_7_segment_display_3 (
    .g(b2d_4_g), .f(b2d_4_f), .a(b2d_4_a_2), .b(b2d_4_b_2), .e(b2d_4_e), .d(b2d_4_d_2), .c(b2d_4_c_2));  // open: dp
  _7_Segment_Display u_7_segment_display_4 (
    .g(b2d_6_g), .f(b2d_6_f), .a(b2d_6_a_2), .b(b2d_6_b_2), .e(b2d_6_e), .d(b2d_6_d_2), .c(b2d_6_c_2));  // open: dp
  _7_Segment_Display u_7_segment_display_5 (
    .g(b2d_3_g), .f(b2d_3_f), .a(b2d_3_a_2), .b(b2d_3_b_2), .e(b2d_3_e), .d(b2d_3_d_2), .c(b2d_3_c_2));  // open: dp
  _7_Segment_Display u_7_segment_display_6 (
    .g(b2d_5_g), .f(b2d_5_f), .a(b2d_5_a_2), .b(b2d_5_b_2), .e(b2d_5_e), .d(b2d_5_d_2), .c(b2d_5_c_2));  // open: dp

  // Notes on the sheet:
  //   SECONDS
  //   MINUTES
  //   HOURS
endmodule

module b2d (
  input  D,
  input  C,
  input  B,
  input  A,
  output a_2,
  output b_2,
  output c_2,
  output d_2,
  output e,
  output f,
  output g
);

  wire and_1_out, and_2_out, and_3_out, and_4_out, and_5_out, and_6_out, and_7_out, and_8_out, and_9_out,
       and_10_out, and_11_out, and_12_out, and_13_out, and_14_out, and_15_out, and_16_out, not_1_out,
       not_2_out, not_3_out, not_4_out, not_5_out, not_6_out, not_7_out, not_8_out, not_9_out, not_10_out,
       not_11_out, not_12_out, not_13_out, not_14_out, not_15_out, not_16_out, not_17_out, not_18_out,
       not_19_out, not_20_out, not_21_out;

  not not_1 (not_1_out, C);
  and and_1 (and_1_out, not_1_out, not_2_out);
  not not_2 (not_2_out, A);
  and and_2 (and_2_out, C, A);
  not not_3 (not_3_out, C);
  not not_4 (not_4_out, B);
  and and_3 (and_3_out, not_4_out, not_5_out);
  not not_5 (not_5_out, A);
  and and_4 (and_4_out, B, A);
  not not_6 (not_6_out, B);
  or or_1 (c_2, not_6_out, A, C);
  not not_7 (not_7_out, C);
  and and_5 (and_5_out, not_7_out, not_8_out);
  not not_8 (not_8_out, A);
  not not_9 (not_9_out, C);
  and and_6 (and_6_out, not_9_out, B);
  and and_7 (and_7_out, B, not_10_out);
  not not_10 (not_10_out, A);
  not not_11 (not_11_out, B);
  and and_8 (and_8_out, C, not_11_out, A);
  not not_12 (not_12_out, C);
  and and_9 (and_9_out, not_12_out, not_13_out);
  not not_13 (not_13_out, A);
  and and_10 (and_10_out, B, not_14_out);
  not not_14 (not_14_out, A);
  not not_15 (not_15_out, B);
  and and_11 (and_11_out, not_15_out, not_16_out);
  not not_16 (not_16_out, A);
  and and_12 (and_12_out, C, not_17_out);
  not not_17 (not_17_out, B);
  and and_13 (and_13_out, C, not_18_out);
  not not_18 (not_18_out, A);
  not not_19 (not_19_out, C);
  and and_14 (and_14_out, not_19_out, B);
  and and_15 (and_15_out, C, not_20_out);
  not not_20 (not_20_out, B);
  and and_16 (and_16_out, C, not_21_out);
  not not_21 (not_21_out, A);
  or or_2 (a_2, and_1_out, B, and_2_out, D);
  or or_3 (b_2, not_3_out, and_3_out, and_4_out);
  or or_4 (d_2, and_5_out, and_6_out, and_7_out, and_8_out, D);
  or or_5 (e, and_9_out, and_10_out);
  or or_6 (f, and_11_out, and_12_out, and_13_out, D);
  or or_7 (g, and_14_out, and_15_out, and_16_out, D);
endmodule
